# Fritzing sketch pH_I2C (saved by Fritzing 0.9.3b)
breadboards: 1

parts:
  Part1 = Arduino Uno (Rev3)
  pH_Circuit1 = pH Circuit

nets:
  N1: Part1.A4/SDA, pH_Circuit1.TX
  N2: Part1.A5/SCL, pH_Circuit1.RX
  GND: Part1.GND, pH_Circuit1.GND
  3V3: Part1.3V3, pH_Circuit1.Vcc
